// Logisim project Demi Additionneur.circ as structural Verilog
// Add-Binaire
module Additionneur (
  input  R_prime,
  input  A,
  input  B,
  output S,
  output R
);

  wire demi_additionneur_1_r, demi_additionneur_1_s, demi_additionneur_2_r;

  Demi_Additionneur demi_additionneur_1 (.A(A), .B(B), .S(demi_additionneur_1_s), .R(demi_additionneur_1_r));
  Demi_Additionneur demi_additionneur_2 (.A(R_prime), .B(demi_additionneur_1_s), .S(S), .R(demi_additionneur_2_r));
  or or_1 (R, demi_additionneur_2_r, demi_additionneur_1_r);
endmodule

// Demi-Add
module Demi_Additionneur (
  input  A,
  input  B,
  output S,
  output R
);

  wire not_1_out, or_1_out;

  or or_1 (or_1_out, A, B);
  not not_1 (not_1_out, R);
  and and_1 (R, B, A);
  and and_2 (S, or_1_out, not_1_out);
endmodule

module Additionneur_4_bit_Parallele (
  input  in_1,
  input  A1,
  input  B1,
  input  A2,
  input  B2,
  input  A3,
  input  B3,
  input  A4,
  input  B4,
  output S1,
  output S2,
  output S3,
  output S4,
  output S5
);

  wire additionneur_1_r, additionneur_2_r, additionneur_3_r;

  Additionneur additionneur_1 (.R_prime(in_1), .A(A1), .B(B1), .S(S1), .R(additionneur_1_r));
  Additionneur additionneur_2 (.R_prime(additionneur_1_r), .A(A2), .B(B2), .S(S2), .R(additionneur_2_r));
  Additionneur additionneur_3 (.R_prime(additionneur_2_r), .A(A3), .B(B3), .S(S3), .R(additionneur_3_r));
  Additionneur additionneur_4 (.R_prime(additionneur_3_r), .A(A4), .B(B4), .S(S4), .R(S5));
endmodule

module \Mémoire  (
  input  in_1,
  input  in_2,
  input  in_3,
  output out_4,
  output out_5
);

  wire or_1_out, or_2_out;

  or or_1 (or_1_out, in_1, in_2);
  or or_2 (or_2_out, in_2, in_3);
  J_K_Flip_Flop j_k_ff_1 (.J(or_1_out), .K(or_2_out), .Q(out_4), .Qn(out_5));  // open: clk, preset, en, reset
endmodule
